# Fritzing sketch IR_Bin_Schaltplan (saved by Fritzing 0.9.4)
breadboards: 1

parts:
  LED1 = LED - 5mm [color="Red (633nm)" package="5 mm [THT]"]
  LED2 = LED - 5mm [color="Red (633nm)" package="5 mm [THT]"]
  LED3 = LED - 5mm [color="Red (633nm)" package="5 mm [THT]"]
  LED4 = LED - 5mm [color="Red (633nm)" package="5 mm [THT]"]
  Bauteil1 = Arduino Uno (Rev3)
  R1 = Resistor [tolerance=±5% resistance=220 package=THT]
  R2 = Resistor [tolerance=±5% resistance=220 package=THT]
  R3 = Resistor [tolerance=±5% resistance=220 package=THT]
  R4 = Resistor [tolerance=±5% resistance=220 package=THT]
  IR1 = TSOP312.., 314.. [package=THT]

nets:
  N1: LED1.cathode, LED2.cathode, LED3.cathode, LED4.cathode, LED4.anode, Bauteil1.GND, IR1.Vs
  N2: LED1.anode, R4.Pin_0
  N3: LED2.anode, R3.Pin_0
  N4: LED3.anode, R2.Pin_0
  N5: Bauteil1.D9_PWM, R3.Pin_1
  N6: Bauteil1.D10_PWM/SS, R4.Pin_1
  N7: Bauteil1.D3_PWM, IR1.GND
  N8: Bauteil1.D5_PWM, R1.Pin_1
  N9: Bauteil1.D6_PWM, R2.Pin_1
  N10: Bauteil1.5V, IR1.Data
