# Fritzing sketch LED_TASTER_Schaltplan (saved by Fritzing 0.9.4)
breadboards: 1

parts:
  LED1 = RGB LED (com. cathode, rgb) [package="5 mm [THT]"]
  U2 = ENCODER_2LED [package=encoder_led_2]
  Bauteil1 = Arduino Uno (Rev3)

nets:
  N1: LED1.red_anode, Bauteil1.D10_PWM/SS
  N2: LED1.common_cathode, Bauteil1.D9_PWM
  N3: LED1.green_anode, Bauteil1.D11_PWM/MOSI
  N4: LED1.blue_anode, Bauteil1.GND
  N5: U2.+G, Bauteil1.D4
  N6: U2.+R, Bauteil1.D5_PWM
  N7: U2.A, Bauteil1.D6_PWM
